# Fritzing sketch Esquematico-Imperial-March (saved by Fritzing 1.0.0rc)
breadboards: 1

parts:
  Piezo1 = Piezo Speaker - PC Mount [part_number=COM-07950]
  LED1 = LED - 5mm [color="White (8000K)" current=0.030A package="5 mm [THT]"]
  LED2 = LED - 5mm [color="Red (633nm)" current=0.030A package="5 mm [THT]"]
  R1 = Resistor [tolerance=±5% resistance=330 package="2512 [SMD]"]
  R2 = Resistor [tolerance=±5% resistance=330 package="2512 [SMD]"]
  Componente1 = Arduino Uno (Rev3)
  Y1 = Resonator [frequency="16 Mhz" package=THT]

nets:
  GND: Piezo1.GND, LED1.cathode, LED2.cathode, Componente1.GND, Y1.1
  N1: Piezo1.VCC, Componente1.D9_PWM, Y1.0
  N2: LED1.anode, R1.Pin_1
  N3: LED2.anode, R2.Pin_1
  N4: R1.Pin_0, Componente1.D13/SCK
  N5: R2.Pin_0, Componente1.D12/MISO

custom parts:
  Piezo Speaker - PC Mount: This is a small 12mm round speaker that operates around the audible 2kHz range. You can use these speakers to create simple music or user interfaces. Each speaker is PTH solderable and requires an operating voltage of 3.5-5V with a mean current of 35mA max. These speakers also have a typical sound output of 95 dBA and a coil resistance of 42 ±6.3 ohms.
